# Fritzing sketch PCB motores (saved by Fritzing 0.9.3b)
circuit board: 6.40087cm x 4.17865cm

parts:
  L293D_F = L293D [package=THT]
  L293D_B = L293D [package=THT]
  Entrada = Battery
  Arduino = Battery
  Motor = Battery
  Motor1 = Battery
  Motor2 = Battery
  Motor3 = Battery
  Motor4 = Battery
  Motor5 = Battery
  Motor6 = Battery
  Motor7 = Battery

nets:
  N1: L293D_F.Enable_1, L293D_F.+Vmotor, L293D_F.Enable_2, L293D_F.+V, L293D_B.Enable_1, L293D_B.+Vmotor, L293D_B.Enable_2, L293D_B.+V, Entrada.+, Arduino.+
  N2: L293D_F.In_1, Motor1.-
  N3: L293D_F.Out_1_(_Controlled_by_Enable_1_), Motor1.+
  N4: L293D_F.0V, L293D_B.0V, Entrada.-, Arduino.-
  N5: L293D_F.Out_2_(_Controlled_by_Enable_1_), Motor.+
  N6: L293D_F.In_2, Motor.-
  N7: L293D_F.In_3, Motor7.-
  N8: L293D_F.Out_3_(_Controlled_by_Enable_2_), Motor7.+
  N9: L293D_F.Out_4_(_Controlled_by_Enable_2_), Motor6.+
  N10: L293D_F.In_4, Motor6.-
  N11: L293D_B.In_1, Motor2.-
  N12: L293D_B.Out_1_(_Controlled_by_Enable_1_), Motor2.+
  N13: L293D_B.Out_2_(_Controlled_by_Enable_1_), Motor3.+
  N14: L293D_B.In_2, Motor3.-
  N15: L293D_B.In_3, Motor4.-
  N16: L293D_B.Out_3_(_Controlled_by_Enable_2_), Motor4.+
  N17: L293D_B.Out_4_(_Controlled_by_Enable_2_), Motor5.+
  N18: L293D_B.In_4, Motor5.-
